// Digital circuit hazard-unit.dig as structural Verilog
module hazard_unit (
  input  [4:0] RR0_2,
  input  [4:0] WR_3,
  input  [4:0] WR_4,
  input  RFW_3,
  input  RFW_4,
  input  [4:0] RR1_2,
  input  MLD_3,
  input  EN,
  input  CLR,
  input  PCbr_2,
  output [1:0] FRD0,
  output [1:0] FRD1,
  output PC_EN,
  output IF_DR_EN,
  output DR_EX_EN,
  output EX_MEM_CLR,
  output EX_DR_CLR,
  output IF_EX_CLR
);

  wire and_1_out, and_2_out, and_3_out, and_4_out, and_5_out, and_6_out, comparator_1_eq, comparator_2_eq,
       comparator_3_eq, comparator_4_eq, comparator_5_eq, comparator_6_eq, comparator_7_eq, comparator_8_eq,
       comparator_9_eq, or_1_out, stall;

  Comparator #(.Bits(5)) comparator_1 (.a(RR0_2), .b(WR_3), .eq(comparator_1_eq));  // open: gt, lt
  Comparator #(.Bits(5)) comparator_2 (.a(RR1_2), .b(WR_3), .eq(comparator_2_eq));  // open: gt, lt
  Comparator comparator_3 (.a(PCbr_2), .b(1'b1), .eq(comparator_3_eq));  // open: gt, lt
  Comparator #(.Bits(5)) comparator_4 (.a(RR0_2), .b(WR_3), .eq(comparator_4_eq));  // open: gt, lt
  Comparator #(.Bits(5)) comparator_5 (.a(RR0_2), .b(WR_4), .eq(comparator_5_eq));  // open: gt, lt
  Comparator #(.Bits(5)) comparator_6 (.a(RR1_2), .b(WR_3), .eq(comparator_6_eq));  // open: gt, lt
  Comparator #(.Bits(5)) comparator_7 (.a(RR1_2), .b(WR_4), .eq(comparator_7_eq));  // open: gt, lt
  Comparator comparator_8 (.a(MLD_3), .b(1'b1), .eq(comparator_8_eq));  // open: gt, lt
  Comparator comparator_9 (.a(RFW_3), .b(1'b1), .eq(comparator_9_eq));  // open: gt, lt
  or or_1 (or_1_out, comparator_1_eq, comparator_2_eq);
  Multiplexer multiplexer_1 (.sel(stall), .in_0(EN), .in_1(1'b0), .out(PC_EN));
  Multiplexer multiplexer_2 (.sel(stall), .in_0(1'b1), .in_1(1'b0), .out(IF_DR_EN));
  Multiplexer multiplexer_3 (.sel(stall), .in_0(1'b1), .in_1(1'b0), .out(DR_EX_EN));
  Multiplexer multiplexer_4 (.sel(stall), .in_0(CLR), .in_1(1'b1), .out(EX_MEM_CLR));
  Multiplexer multiplexer_5 (.sel(comparator_3_eq), .in_0(CLR), .in_1(1'b1), .out(IF_EX_CLR));
  Multiplexer multiplexer_6 (.sel(comparator_3_eq), .in_0(CLR), .in_1(1'b1), .out(EX_DR_CLR));
  and and_1 (and_1_out, comparator_4_eq, RFW_3);
  and and_2 (and_2_out, comparator_5_eq, RFW_4);
  and and_3 (and_3_out, comparator_6_eq, RFW_3);
  and and_4 (and_4_out, comparator_7_eq, RFW_4);
  and and_5 (and_5_out, ~and_1_out, ~and_2_out);  // And
  and and_6 (and_6_out, ~and_3_out, ~and_4_out);  // And
  and and_7 (stall, comparator_8_eq, comparator_9_eq, or_1_out);
  PriorityEncoder #(.Selector_Bits(2)) priorityencoder_1 (
    .in0(and_5_out), .in1(and_2_out), .in2(and_1_out), .in3(1'b0), .num(FRD0));  // open: any
  PriorityEncoder #(.Selector_Bits(2)) priorityencoder_2 (
    .in0(and_6_out), .in1(and_4_out), .in2(and_3_out), .in3(1'b0), .num(FRD1));  // open: any
endmodule
