// Digital circuit main.dig as structural Verilog
module main (
  input  [4:0] PROG,
  input  CLK,
  input  CLR,
  input  EN,
  output [63:0] A0,
  output [63:0] A1,
  output [63:0] A2,
  output DONE,
  output [63:0] zero,
  output [63:0] ra,
  output [63:0] sp,
  output [63:0] gp,
  output [63:0] tp,
  output [63:0] t0,
  output [63:0] t1,
  output [63:0] t2,
  output [63:0] s0_fp,
  output [63:0] s1,
  output [63:0] a0_2,
  output [63:0] a1_2,
  output [63:0] a2_2,
  output [63:0] a3,
  output [63:0] a4,
  output [63:0] a5,
  output [63:0] a6,
  output [63:0] a7,
  output [63:0] s2,
  output [63:0] s3,
  output [63:0] s4,
  output [63:0] s5,
  output [63:0] s6,
  output [63:0] s7,
  output [63:0] s8,
  output [63:0] s9,
  output [63:0] s10,
  output [63:0] s11,
  output [63:0] t3,
  output [63:0] t4,
  output [63:0] t5,
  output [63:0] t6
);

  wire _01_dr_ex_register_1_p27, _02_ex_mem_register_1_p21, ALOp_1, ALOp_2, ALUA_1, ALUA_2, ALUB_1,
       and_2_out, BUOp_1, BUOp_2, CLK_t, DR_EX_EN, EX_DR_CLR, EX_MEM_CLR, IF_DR_EN, IF_EX_CLR, iw_0, iw_1,
       iw_2, iw_3, iw_to_ascii_1_p2, iw_to_ascii_1_p3, iw_to_ascii_1_p4, iw_to_ascii_1_p5, iw_to_ascii_2_p2,
       iw_to_ascii_2_p3, iw_to_ascii_2_p4, iw_to_ascii_2_p5, iw_to_ascii_3_p2, iw_to_ascii_3_p3,
       iw_to_ascii_3_p4, iw_to_ascii_3_p5, iw_to_ascii_4_p2, iw_to_ascii_4_p3, iw_to_ascii_4_p4,
       iw_to_ascii_4_p5, iw_to_ascii_5_p2, iw_to_ascii_5_p3, iw_to_ascii_5_p4, iw_to_ascii_5_p5,
       mem_inst_1_p8, mem_inst_1_p9, MLD_1, MLD_2, MLD_3, MR_1, MR_2, MR_3, MR_4, MST_1, MST_2, MST_3, MSZ_1,
       MSZ_2, MSZ_3, not_1_out, PC_EN, PCbr_2, PCbr_3, PCbr_4, PCsl_1, PCsl_2, register_file_1_p8,
       register_file_1_p9, RFW_1, RFW_2, RFW_3, RFW_4, RR0_1, RR0_3, RR0_4, RR1_1, RR1_3, RR1_4, WDsl_1,
       WDsl_2, WDsl_3, WDsl_4, WR_1, WR_2;
  wire [1:0] FRD0, FRD1;
  wire [2:0] ALUB_2;
  wire [4:0] RR0_2, RR1_2, WR_3, WR_4;
  wire [31:0] iw_4;
  wire [63:0] _01_dr_ex_register_1_p24, _01_dr_ex_register_1_p25, _01_dr_ex_register_1_p26,
       _02_ex_mem_register_1_p19, _02_ex_mem_register_1_p20, _03_mem_wb_register_1_p16,
       _03_mem_wb_register_1_p17, _03_mem_wb_register_1_p18, alu_1_p4, decoder_imm_1_p6, decoder_imm_1_p7,
       decoder_imm_1_p8, decoder_imm_1_p9, decoder_imm_1_p10, decoder_imm_1_p11, multiplexer_1_out,
       multiplexer_2_out, multiplexer_3_out, multiplexer_4_out, multiplexer_5_out, multiplexer_6_out,
       multiplexer_7_out, PC, PC_plus_4_s, ramdualport_1_d;

  Multiplexer #(.Bits(64)) multiplexer_1 (.sel(PCbr_2), .in_0(PC_plus_4_s), .in_1(alu_1_p4), .out(multiplexer_1_out));
  // register_with_clr_64bits PC: pin names not known; wires that end beside it: multiplexer_1_out, CLK_t, PC_EN, CLR, PC
  and and_1 (CLK_t, CLK, ~DONE);  // And
  Comparator #(.Bits(32)) End (.a(iw_4), .b(32'hc0001073), .eq(DONE));  // open: gt, lt
  LED led_1 (.in(DONE));
  Add #(.Bits(64)) PC_plus_4 (.a(PC), .b(64'h4), .c_i(1'b0), .s(PC_plus_4_s));  // open: c_o
  // Probe on iw_to_ascii_1_p2
  // iw_to_ascii iw_to_ascii_1: pin names not known; wires that end beside it: iw_0, iw_to_ascii_1_p2, iw_to_ascii_1_p3, iw_to_ascii_1_p4, iw_to_ascii_1_p5
  // mem_inst mem_inst_1: pin names not known; wires that end beside it: PROG, PC[9:2], iw_0, PC, PC_plus_4_s, CLK_t, IF_DR_EN, mem_inst_1_p8, mem_inst_1_p9
  // Probe on iw_to_ascii_1_p4
  // Probe on iw_to_ascii_1_p3
  // Probe on iw_to_ascii_1_p5
  // _00_IF_DR_register _00_if_dr_register_1: pin names not known; wires that end beside it: iw_0, iw_1
  // decoder_inst decoder_inst_1: pin names not known; wires that end beside it: iw_1, MSZ_1, MST_1, MLD_1, MR_1, BUOp_1, WDsl_1, PCsl_1, ALUB_1, ALUA_1, ALOp_1, RFW_1
  // decoder_reg decoder_reg_1: pin names not known; wires that end beside it: iw_1, RR0_1, RR1_1, WR_1
  Multiplexer #(.Bits(64)) multiplexer_2 (
    .sel(WDsl_4), .in_0(multiplexer_7_out), .in_1(_03_mem_wb_register_1_p18), .out(multiplexer_2_out));
  and and_2 (and_2_out, RFW_4, EN);
  not not_1 (not_1_out, CLK_t);
  // Probe on iw_to_ascii_2_p2
  // iw_to_ascii iw_to_ascii_2: pin names not known; wires that end beside it: iw_1, iw_to_ascii_2_p2, iw_to_ascii_2_p3, iw_to_ascii_2_p4, iw_to_ascii_2_p5
  // register_file register_file_1: pin names not known; wires that end beside it: RR0_1, RR1_1, WR_4, and_2_out, multiplexer_2_out, not_1_out, CLR, register_file_1_p8, register_file_1_p9, zero, ra, sp, gp, tp, t0, t1, t2, s0_fp, s1, A0, A1, A2, a3, a4, a5, a6, a7, s2, s3, s4, s5, s6
  // Probe on iw_to_ascii_2_p4
  // Probe on iw_to_ascii_2_p3
  // Probe on iw_to_ascii_2_p5
  // _01_DR_EX_register _01_dr_ex_register_1: pin names not known; wires that end beside it: iw_1, RR0_1, RR1_1, WR_1, register_file_1_p8, register_file_1_p9, mem_inst_1_p8, mem_inst_1_p9, MSZ_1, MST_1, MLD_1, MR_1, BUOp_1, WDsl_1, PCsl_1, ALUB_1, ALUA_1, ALOp_1, RFW_1, iw_2, RR0_2, RR1_2, WR_2, _01_dr_ex_register_1_p24, _01_dr_ex_register_1_p25, _01_dr_ex_register_1_p26, _01_dr_ex_register_1_p27, MSZ_2, MST_2, MLD_2, MR_2, BUOp_2, WDsl_2, PCsl_2, ALUB_2
  hazard_unit hazard_unit_1 (
    .RR0_2(RR0_2), .WR_3(WR_3), .WR_4(WR_4), .RFW_3(RFW_3), .RFW_4(RFW_4), .RR1_2(RR1_2), .MLD_3(MLD_3),
    .EN(EN), .CLR(CLR), .PCbr_2(PCbr_2), .FRD0(FRD0), .FRD1(FRD1), .PC_EN(PC_EN), .IF_DR_EN(IF_DR_EN),
    .DR_EX_EN(DR_EX_EN), .EX_MEM_CLR(EX_MEM_CLR), .IF_EX_CLR(EX_DR_CLR), .EX_DR_CLR(IF_EX_CLR));
  Multiplexer #(.Selector_Bits(2), .Bits(64)) multiplexer_3 (
    .sel(FRD0), .in_0(_01_dr_ex_register_1_p24), .in_1(multiplexer_7_out), .in_2(_02_ex_mem_register_1_p19),
    .in_3(_02_ex_mem_register_1_p19), .out(multiplexer_3_out));
  // decoder_imm decoder_imm_1: pin names not known; wires that end beside it: EX_DR_CLR, ALUA_2, ALOp_2, RFW_2, iw_2, decoder_imm_1_p6, decoder_imm_1_p7, decoder_imm_1_p8, decoder_imm_1_p9, decoder_imm_1_p10, decoder_imm_1_p11
  Multiplexer #(.Selector_Bits(2), .Bits(64)) multiplexer_4 (
    .sel(FRD1), .in_0(_01_dr_ex_register_1_p25), .in_1(multiplexer_7_out), .in_2(_02_ex_mem_register_1_p19),
    .in_3(_02_ex_mem_register_1_p19), .out(multiplexer_4_out));
  // Probe on iw_to_ascii_3_p2
  // iw_to_ascii iw_to_ascii_3: pin names not known; wires that end beside it: iw_2, iw_to_ascii_3_p2, iw_to_ascii_3_p3, iw_to_ascii_3_p4, iw_to_ascii_3_p5
  // Probe on iw_to_ascii_3_p4
  // Probe on iw_to_ascii_3_p3
  // branch_unit branch_unit_1: pin names not known; wires that end beside it: multiplexer_3_out, multiplexer_4_out, PCsl_2, BUOp_2, PCbr_2
  Multiplexer #(.Bits(64)) multiplexer_5 (
    .sel(ALUA_2), .in_0(multiplexer_3_out), .in_1(_01_dr_ex_register_1_p26), .out(multiplexer_5_out));
  Multiplexer #(.Selector_Bits(3), .Bits(64)) multiplexer_6 (
    .sel(ALUB_2), .in_0(multiplexer_4_out), .in_1(decoder_imm_1_p6), .in_2(decoder_imm_1_p10),
    .in_3(decoder_imm_1_p9), .in_4(decoder_imm_1_p8), .in_5(decoder_imm_1_p11), .in_6(decoder_imm_1_p7),
    .in_7({64{1'b0}}), .out(multiplexer_6_out));
  // Probe on iw_to_ascii_3_p5
  // alu alu_1: pin names not known; wires that end beside it: multiplexer_5_out, multiplexer_6_out, ALOp_2, alu_1_p4
  // _02_EX_MEM_register _02_ex_mem_register_1: pin names not known; wires that end beside it: iw_2, RR0_2, RR1_2, WR_2, alu_1_p4, multiplexer_4_out, _01_dr_ex_register_1_p27, MSZ_2, MST_2, MLD_2, MR_2, WDsl_2, PCbr_2, RFW_2, iw_3, RR0_3, RR1_3, WR_3, _02_ex_mem_register_1_p19, _02_ex_mem_register_1_p20, _02_ex_mem_register_1_p21, MSZ_3, MST_3, MLD_3, MR_3
  // Probe on iw_to_ascii_4_p2
  // iw_to_ascii iw_to_ascii_4: pin names not known; wires that end beside it: iw_3, iw_to_ascii_4_p2, iw_to_ascii_4_p3, iw_to_ascii_4_p4, iw_to_ascii_4_p5
  RAMDualPort #(.AddrBits(7), .Bits(64)) ramdualport_1 (
    .A(_02_ex_mem_register_1_p19[9:3]), .Din(_02_ex_mem_register_1_p20), .str(MST_3), .C(CLK_t), .ld(MLD_3),
    .D(ramdualport_1_d));
  // Probe on iw_to_ascii_4_p4
  // Probe on iw_to_ascii_4_p3
  // Probe on iw_to_ascii_4_p5
  // _03_MEM_WB_register _03_mem_wb_register_1: pin names not known; wires that end beside it: iw_3, RR0_3, RR1_3, WR_3, _02_ex_mem_register_1_p19, ramdualport_1_d, _02_ex_mem_register_1_p21, MR_3, WDsl_3, PCbr_3, RFW_3, iw_4, RR0_4, RR1_4, WR_4, _03_mem_wb_register_1_p16, _03_mem_wb_register_1_p17, _03_mem_wb_register_1_p18, MR_4, WDsl_4, PCbr_4
  // Probe on iw_to_ascii_5_p2
  // iw_to_ascii iw_to_ascii_5: pin names not known; wires that end beside it: iw_4, iw_to_ascii_5_p2, iw_to_ascii_5_p3, iw_to_ascii_5_p4, iw_to_ascii_5_p5
  Multiplexer #(.Bits(64)) multiplexer_7 (
    .sel(MR_4), .in_0(_03_mem_wb_register_1_p16), .in_1(_03_mem_wb_register_1_p17), .out(multiplexer_7_out));
  // Probe on iw_to_ascii_5_p4
  // Probe on iw_to_ascii_5_p3
  // Probe on iw_to_ascii_5_p5

  assign a0_2 = A0;
  assign a1_2 = A1;
  assign a2_2 = A2;

  // Other names for the same wires on the sheet: x0[63:0] = zero; x1[63:0] = ra; x2[63:0] = sp; x3[63:0] = gp;
  //   x4[63:0] = tp; x5[63:0] = t0; x6[63:0] = t1; x7[63:0] = t2; x8[63:0] = s0_fp; x9[63:0] = s1; x10[63:0] = A0;
  //   x11[63:0] = A1; x12[63:0] = A2; x13[63:0] = a3; x14[63:0] = a4; x15[63:0] = a5; x16[63:0] = a6; x17[63:0] = a7;
  //   x18[63:0] = s2; x19[63:0] = s3; x20[63:0] = s4; x21[63:0] = s5; x22[63:0] = s6; x23[63:0] = s7; x24[63:0] = s8;
  //   x25[63:0] = s9; x26[63:0] = s10; x27[63:0] = s11; x28[63:0] = t3; x29[63:0] = t4; x30[63:0] = t6;
  //   x31[63:0] = t5

  // Notes on the sheet:
  //   CLK: Hz: 2147483647
  //   (0) IF Stage
  //   Instruction Fetch
  //   (1) DR Stage
  //   Decode Register Read
  //   (2) EX Stage
  //   Execute
  //   (3) MEM Stage
  //   Memory
  //   (4) WB Stage
  //   Write Back
endmodule

/* Test case 00-add-3nop-test:
EN CLR CLK PROG A0 DONE
1  1   0   x    x  x
1  0   0   x    x  x
while (!(DONE))
1  0   C   0    x  x
end while
1  0   0   0    4  1
*/

/* Test case 02-jal-test:
EN CLR CLK PROG A0 DONE
1  1   0   x    x  x
1  0   0   x    x  x
while (!(DONE))
1  0   C   2    x  x
end while
1  0   0   0    4  1
*/

/* Test case 04-add-fwd-test:
EN CLR CLK PROG A0 DONE
1  1   0   x    x  x
1  0   0   x    x  x
while (!(DONE))
1  0   C   4    x  x
end while
1  0   0   0    3  1
*/

/* Test case 06-jal-fls-test:
EN CLR CLK PROG A0 DONE
1  1   0   x    x  x
1  0   0   x    x  x
while (!(DONE))
1  0   C   6    x  x
end while
1  0   0   0    6  1
*/

/* Test case 01-add-2nop-test:
EN CLR CLK PROG A0 DONE
1  1   0   x    x  x
1  0   0   x    x  x
while (!(DONE))
1  0   C   1    x  x
end while
1  0   0   0    4  1
*/

/* Test case 03-ld-test:
EN CLR CLK PROG A0 DONE
1  1   0   x    x  x
1  0   0   x    x  x
while (!(DONE))
1  0   C   3    x  x
end while
1  0   0   0    100 1
*/

/* Test case 05-ld-stl-test:
EN CLR CLK PROG A0 DONE
1  1   0   x    x  x
1  0   0   x    x  x
while (!(DONE))
1  0   C   5    x  x
end while
1  0   0   0    2  1
*/
